// Logisim project 8bit_8Registor.circ as structural Verilog: 2 circuits, main circuit 8bit_8Registor
// Register
module _8bit_8Registor (
  input  [3:0] RegD,
  input  [3:0] RegB,
  input  [3:0] RegA,
  input  WriteEnable,
  input  [7:0] Data,
  input  Clock,
  input  Reset,
  output [7:0] BusA,
  output [7:0] BusB
);

  wire demultiplexer_1_out1, demultiplexer_1_out2, demultiplexer_1_out3, demultiplexer_1_out4,
       demultiplexer_1_out5, demultiplexer_1_out6, demultiplexer_1_out7;
  wire [7:0] gp_q, sp_q, t0_q, t1_q, t2_q, t3_q, t4_q, zero_q;

  Demultiplexer #(.select(3)) demultiplexer_1 (
    .out1(demultiplexer_1_out1), .out2(demultiplexer_1_out2), .out3(demultiplexer_1_out3),
    .out4(demultiplexer_1_out4), .out5(demultiplexer_1_out5), .out6(demultiplexer_1_out6),
    .out7(demultiplexer_1_out7), .in(WriteEnable), .sel(RegD[2:0]));  // open: out0, en
  Register zero (.D(Data), .en(1'b0), .Q(zero_q), .clk(Clock), .clr(Reset));
  Register t1 (.D(Data), .en(demultiplexer_1_out2), .Q(t1_q), .clk(Clock), .clr(Reset));
  Register t3 (.D(Data), .en(demultiplexer_1_out4), .Q(t3_q), .clk(Clock), .clr(Reset));
  Register sp (.D(Data), .en(demultiplexer_1_out6), .Q(sp_q), .clk(Clock), .clr(Reset));
  Register t0 (.D(Data), .en(demultiplexer_1_out1), .Q(t0_q), .clk(Clock), .clr(Reset));
  Register t2 (.D(Data), .en(demultiplexer_1_out3), .Q(t2_q), .clk(Clock), .clr(Reset));
  Register t4 (.D(Data), .en(demultiplexer_1_out5), .Q(t4_q), .clk(Clock), .clr(Reset));
  Register gp (.D(Data), .en(demultiplexer_1_out7), .Q(gp_q), .clk(Clock), .clr(Reset));
  Multiplexer #(.select(3), .width(8)) multiplexer_1 (
    .in0(zero_q), .in1(t0_q), .in2(t1_q), .in3(t2_q), .in4(t3_q), .in5(t4_q), .in6(sp_q), .in7(gp_q),
    .out(BusA), .sel(RegA[2:0]));  // open: en
  Multiplexer #(.select(3), .width(8)) multiplexer_2 (
    .in0(zero_q), .in1(t0_q), .in2(t1_q), .in3(t2_q), .in4(t3_q), .in5(t4_q), .in6(sp_q), .in7(gp_q),
    .out(BusB), .sel(RegB[2:0]));  // open: en
endmodule

module test (
  input  [3:0] in_1,
  input  [3:0] in_2,
  input  [3:0] in_3,
  input  in_4,
  input  [7:0] in_5,
  input  in_6,
  output [7:0] out_7,
  output [7:0] out_8
);

  wire clock_1_out;

  Clock clock_1 (.out(clock_1_out));
  _8bit_8Registor u_8bit_8registor_1 (
    .WriteEnable(in_4), .Data(in_5), .Clock(clock_1_out), .BusA(out_7), .BusB(out_8), .RegD(in_1),
    .RegB(in_2), .RegA(in_3), .Reset(in_6));
endmodule
