// Logisim project ALU_control.circ as structural Verilog: 1 circuit, main circuit ALU_ctrl
module ALU_ctrl (
  input  [3:0] in_1,
  output [3:0] out_2
);

  wire and_1_out, nor_1_out, not_1_out, xor_1_out;

  and and_1 (and_1_out, in_1[0], in_1[1]);
  nor nor_1 (nor_1_out, in_1[0], in_1[1]);
  xor xor_1 (xor_1_out, in_1[0], in_1[1]);
  not not_1 (not_1_out, and_1_out);
  Multiplexer #(.select(2)) multiplexer_1 (
    .in0(nor_1_out), .in1(and_1_out), .in2(1'b0), .in3(1'b0), .out(out_2[3]), .sel(in_1[3:2]), .en(1'b1));
  Multiplexer #(.select(2)) multiplexer_2 (
    .in0(nor_1_out), .in1(and_1_out), .in2(and_1_out), .in3(1'b0), .out(out_2[2]), .sel(in_1[3:2]), .en(1'b1));
  Multiplexer #(.select(2)) multiplexer_3 (
    .in0(nor_1_out), .in1(1'b0), .in2(xor_1_out), .in3(xor_1_out), .out(out_2[1]), .sel(in_1[3:2]), .en(1'b1));
  Multiplexer #(.select(2)) multiplexer_4 (
    .in0(xor_1_out), .in1(and_1_out), .in2(not_1_out), .in3(nor_1_out), .out(out_2[0]), .sel(in_1[3:2]),
    .en(1'b1));
endmodule
