// Logisim project ALU_wrap.circ as structural Verilog: 2 circuits, main circuit ALU mod
module ALU_mod (
  input  [7:0] A,
  input  [7:0] B,
  input  [3:0] in_3,
  output Zero,
  output [7:0] Result,
  output OverFlow
);

  wire [7:0] multiplexer_1_out, multiplexer_2_out;

  Multiplexer #(.width(8)) multiplexer_1 (.in0(A), .in1(B), .out(multiplexer_1_out), .sel(in_3[3]), .en(1'b1));
  Multiplexer #(.width(8)) multiplexer_2 (.in0(B), .in1(A), .out(multiplexer_2_out), .sel(in_3[3]), .en(1'b1));
  // ALU_8_by_ART alu_8_by_art_1: pin names not known; wires that end beside it: multiplexer_1_out, multiplexer_2_out, in_3[2:0], Zero, Result, OverFlow
endmodule

module test (
);

  ALU_mod alu_mod_1 ();  // open: A, B, Zero, Result, OverFlow, in_3
endmodule
