// Logisim project Instruction_Decode.circ as structural Verilog: 2 circuits, main circuit Instruction Splitter
// instruction handle
module Instruction_Splitter (
  input  [19:0] instruction,
  output Jump,
  output [3:0] OP_code,
  output [3:0] R_s,
  output [3:0] R_t,
  output [3:0] R_d,
  output [7:0] Immidiate
);

  Multiplexer #(.width(16)) multiplexer_1 (
    .in0(instruction[15:0]), .in1({instruction[7:0], instruction[15:8]}), .out({R_s, R_t, Immidiate}),
    .sel(Jump), .en(1'b1));
  is_jump is_jump_1 (.in_1(instruction[19:16]), .J(Jump));

  assign OP_code = instruction[19:16];
  assign R_d = Immidiate[7:4];

  // Notes on the sheet:
  //   OP code
endmodule

// Jump?
module is_jump (
  input  [3:0] in_1,
  output J
);

  wire not_1_out, not_2_out;

  not not_1 (not_1_out, in_1[2]);
  not not_2 (not_2_out, in_1[3]);
  and and_1 (J, in_1[0], in_1[1], not_1_out, not_2_out);
endmodule
