// Logisim project pipeline_components.circ as structural Verilog: 8 circuits, main circuit main
module main (
);

  control_manipulator_EX control_manipulator_ex_1 ();  // open: J_MR_MW_ne_b_ALUSrc_Rsrc_RW, MemR_MemW_RegW_RegDataSrc, Write_Control_Disable
  piped_pc_control piped_pc_control_1 ();  // open: Curr_PC, Final_PC, BranchPC, Taken, PC_1
  ID id_1 ();  // open: in_1, clock, Rd, Rt, Rs, Rs_Value, Rt_Value, Im, Register_Write, Register_Data_In, Data_Destiantion_Rd, J, MemRead, MemWrite, branch_ne_b, ALU_src, Reg_Src__ALU_1, RegWrite, Reset, ALU_Op
  piped_branch_ctrl piped_branch_ctrl_1 ();  // open: Branch_PC, Taken, PC_1, in_2, in_3, J, neq, branch, Im
  EX ex_1 ();  // open: Rs, Rt, Im, ALU_out, _2_Fwd_Src, _1_Fwd_Src, ALU_src, Fwd_ALU_result, Fwd_Mem_Data, ALU_OP
endmodule

module ID (
  input  [19:0] in_1,
  input  Register_Write,
  input  clock,
  input  [7:0] Register_Data_In,
  input  [3:0] Data_Destiantion_Rd,
  input  Reset,
  output [1:0] branch_ne_b,
  output J,
  output MemRead,
  output MemWrite,
  output ALU_src,
  output Reg_Src__ALU_1,
  output RegWrite,
  output [3:0] Rd,
  output [3:0] Rt,
  output [3:0] Rs,
  output [7:0] Rs_Value,
  output [7:0] Rt_Value,
  output [7:0] Im,
  output [3:0] ALU_Op
);

  wire ctrl_unit_1_regdest, not_1_out;
  wire [3:0] instruction_splitter_1_op_code, instruction_splitter_1_r_d;

  not not_1 (not_1_out, clock);
  Instruction_Splitter instruction_splitter_1 (
    .instruction(in_1), .OP_code(instruction_splitter_1_op_code), .R_s(Rs), .R_t(Rt),
    .R_d(instruction_splitter_1_r_d), .Immidiate(Im), .Jump(J));
  ctrl_unit ctrl_unit_1 (
    .in_1(instruction_splitter_1_op_code), .Branch_X3b(branch_ne_b), .regWrite(RegWrite),
    .regDataSrc(Reg_Src__ALU_1), .MemRad(MemRead), .MemWrite(MemWrite), .RegDest(ctrl_unit_1_regdest),
    .ALUsrc(ALU_src));
  Multiplexer #(.width(4)) multiplexer_1 (
    .in0(instruction_splitter_1_r_d), .in1(Rt), .out(Rd), .sel(ctrl_unit_1_regdest), .en(1'b1));
  _8bit_8Registor u_8bit_8registor_1 (
    .WriteEnable(Register_Write), .Data(Register_Data_In), .Clock(not_1_out), .BusA(Rs_Value),
    .BusB(Rt_Value), .RegD(Data_Destiantion_Rd), .RegB(Rt), .RegA(Rs), .Reset(Reset));
  ALU_ctrl alu_ctrl_1 (.in_1(instruction_splitter_1_op_code), .out_2(ALU_Op));
endmodule

module EX (
  input  ALU_src,
  input  [7:0] Rs,
  input  [7:0] Rt,
  input  [7:0] Im,
  input  [1:0] _2_Fwd_Src,
  input  [3:0] ALU_OP,
  input  [1:0] _1_Fwd_Src,
  input  [7:0] Fwd_ALU_result,
  input  [7:0] Fwd_Mem_Data,
  output [7:0] ALU_out
);

  wire [0:0] multiplexer_3_out;
  wire [7:0] multiplexer_1_out, multiplexer_2_out;

  Multiplexer #(.select(2), .width(8), .enable("false")) multiplexer_1 (
    .in0(Rs), .in1(Rs), .in2(Fwd_ALU_result), .in3(Fwd_Mem_Data), .out(multiplexer_1_out), .sel(_1_Fwd_Src));
  Multiplexer #(.select(2), .width(8), .enable("false")) multiplexer_2 (
    .in0(Rt), .in1(Im), .in2(Fwd_ALU_result), .in3(Fwd_Mem_Data), .out(multiplexer_2_out),
    .sel({_2_Fwd_Src[1], multiplexer_3_out[0]}));
  ALU_mod alu_mod_1 (
    .A(multiplexer_1_out), .B(multiplexer_2_out), .Result(ALU_out), .in_3(ALU_OP));  // open: Zero, OverFlow
  Multiplexer #(.enable("false")) multiplexer_3 (
    .in0(ALU_src), .in1(_2_Fwd_Src[0]), .out(multiplexer_3_out[0]), .sel(_2_Fwd_Src[1]));
endmodule

module control_manipulator_EX (
  input  Write_Control_Disable,
  input  [7:0] J_MR_MW_ne_b_ALUSrc_Rsrc_RW,
  output [3:0] MemR_MemW_RegW_RegDataSrc
);

  wire not_1_out;

  not not_1 (not_1_out, Write_Control_Disable);
  and and_1 (MemR_MemW_RegW_RegDataSrc[1], not_1_out, J_MR_MW_ne_b_ALUSrc_Rsrc_RW[0]);
  and and_2 (MemR_MemW_RegW_RegDataSrc[2], J_MR_MW_ne_b_ALUSrc_Rsrc_RW[5], not_1_out);

  assign {MemR_MemW_RegW_RegDataSrc[3], MemR_MemW_RegW_RegDataSrc[0]} = {J_MR_MW_ne_b_ALUSrc_Rsrc_RW[6], J_MR_MW_ne_b_ALUSrc_Rsrc_RW[1]};
endmodule

// PC ctrl
module piped_pc_control (
  input  [7:0] Curr_PC,
  input  [7:0] BranchPC,
  input  Taken,
  output [7:0] Final_PC,
  output [7:0] PC_1
);

  Adder adder_1 (.a(Curr_PC), .b(8'h1), .out(PC_1));  // open: cin, cout
  Multiplexer #(.width(8), .enable("false")) multiplexer_1 (.in0(PC_1), .in1(BranchPC), .out(Final_PC), .sel(Taken));
endmodule

// Branch Ctrl
module piped_branch_ctrl (
  input  [7:0] PC_1,
  input  [7:0] in_2,
  input  [7:0] in_3,
  input  J,
  input  neq,
  input  branch,
  input  [7:0] Im,
  output [7:0] Branch_PC,
  output Taken
);

  wire and_1_out, is_equal_1_out_3, xor_1_out;
  wire [7:0] adder_1_out;

  or or_1 (Taken, and_1_out, J);
  Multiplexer #(.width(8), .enable("false")) multiplexer_1 (.in0(adder_1_out), .in1(Im), .out(Branch_PC), .sel(J));
  and and_1 (and_1_out, branch, xor_1_out);
  xor xor_1 (xor_1_out, neq, is_equal_1_out_3);
  Adder adder_1 (.a(PC_1), .b(Im), .out(adder_1_out));  // open: cin, cout
  is_equal is_equal_1 (.out_3(is_equal_1_out_3), .A(in_3), .B(in_2));
endmodule

// ==?
module is_equal (
  input  [7:0] A,
  input  [7:0] B,
  output out_3
);

  wire [7:0] xor_1_out;

  nor nor_1 (out_3, xor_1_out[7], xor_1_out[6], xor_1_out[5], xor_1_out[4], xor_1_out[2], xor_1_out[1], xor_1_out[0], xor_1_out[3]);
  assign xor_1_out = A ^ B;  // XOR_Gate xor_1, 8 bits wide
endmodule

module control_manioulator_ID (
  input  Write_Control_Disable,
  input  [7:0] J_MR_MW_ne_b_ALUSrc_Rsrc_RW,
  output [7:0] J_MR_MW_ne_b_ALUSrc_Rsrc_RW_2
);

  wire not_1_out;

  not not_1 (not_1_out, Write_Control_Disable);
  and and_1 (J_MR_MW_ne_b_ALUSrc_Rsrc_RW_2[0], not_1_out, J_MR_MW_ne_b_ALUSrc_Rsrc_RW[0]);
  and and_2 (J_MR_MW_ne_b_ALUSrc_Rsrc_RW_2[5], not_1_out, J_MR_MW_ne_b_ALUSrc_Rsrc_RW[5]);

  assign {J_MR_MW_ne_b_ALUSrc_Rsrc_RW_2[7:6], J_MR_MW_ne_b_ALUSrc_Rsrc_RW_2[4:1]} = {J_MR_MW_ne_b_ALUSrc_Rsrc_RW[7:6], J_MR_MW_ne_b_ALUSrc_Rsrc_RW[4:1]};
endmodule
