// Logisim project pipeline_registers.circ as structural Verilog
module main (
);

  ID_EX id_ex_1 ();  // open: Next_PC, J_MR_MW_ne_b_ALUSrc_Rsrc_RW, RD_RF_RS, Vals_RS_RT_IM, ALU_op, Clock, Next_PC_2, J_MR_MW_ne_b_ALUSrc_Rsrc_RW_2, RD_RF_RS_2, Vals_RS_RT_IM_2, ALU_op_2, Reset
  IF_ID if_id_1 ();  // open: Instruction, clock, Instruction_out, control, Reset, Next_PC, Next_PC_2
  Ex_MEM ex_mem_1 ();  // open: MemR_MemW_RegW_RegDataSrc, ALU_out, MemData, Rd, MemR_MemW_RegW_RegDataSrc_2, ALU_out_2, MemData_2, Rd_2, Clock, Reset
  MEM_WB mem_wb_1 ();  // open: RW_RSrc, ALU_Data, Mem_Data, Rd, Clock, RegW_RegDataSrc, ALU_Data_2, Mem_Data_2, Rd_2, Reset
endmodule

// IF ID
module IF_ID (
  input  control,
  input  [7:0] Next_PC,
  input  [19:0] Instruction,
  input  Reset,
  input  clock,
  output [7:0] Next_PC_2,
  output [19:0] Instruction_out
);

  Register #(.width(28)) register_1 (
    .D({Instruction, Next_PC}), .en(control), .Q({Instruction_out, Next_PC_2}), .clk(clock), .clr(Reset));
endmodule

module ID_EX (
  input  [7:0] Next_PC,
  input  [7:0] J_MR_MW_ne_b_ALUSrc_Rsrc_RW,
  input  [11:0] RD_RF_RS,
  input  [23:0] Vals_RS_RT_IM,
  input  [3:0] ALU_op,
  input  Reset,
  input  Clock,
  output [7:0] Next_PC_2,
  output [7:0] J_MR_MW_ne_b_ALUSrc_Rsrc_RW_2,
  output [11:0] RD_RF_RS_2,
  output [23:0] Vals_RS_RT_IM_2,
  output [3:0] ALU_op_2
);

  Register #(.width(28)) register_1 (
    .D({RD_RF_RS, J_MR_MW_ne_b_ALUSrc_Rsrc_RW, Next_PC}), .en(1'b1),
    .Q({RD_RF_RS_2, J_MR_MW_ne_b_ALUSrc_Rsrc_RW_2, Next_PC_2}), .clk(Clock), .clr(Reset));
  Register #(.width(28)) register_2 (
    .D({ALU_op, Vals_RS_RT_IM}), .en(1'b1), .Q({ALU_op_2, Vals_RS_RT_IM_2}), .clk(Clock), .clr(Reset));
endmodule

// EX MEM
module Ex_MEM (
  input  [3:0] MemR_MemW_RegW_RegDataSrc,
  input  [7:0] ALU_out,
  input  [7:0] MemData,
  input  [3:0] Rd,
  input  Clock,
  input  Reset,
  output [3:0] MemR_MemW_RegW_RegDataSrc_2,
  output [7:0] ALU_out_2,
  output [7:0] MemData_2,
  output [3:0] Rd_2
);

  Register #(.width(24)) register_1 (
    .D({Rd, MemData, ALU_out, MemR_MemW_RegW_RegDataSrc}), .en(1'b1),
    .Q({Rd_2, MemData_2, ALU_out_2, MemR_MemW_RegW_RegDataSrc_2}), .clk(Clock), .clr(Reset));
endmodule

// MEM / WB .
module MEM_WB (
  input  [1:0] RW_RSrc,
  input  [7:0] ALU_Data,
  input  [7:0] Mem_Data,
  input  [3:0] Rd,
  input  Clock,
  input  Reset,
  output [1:0] RegW_RegDataSrc,
  output [7:0] ALU_Data_2,
  output [7:0] Mem_Data_2,
  output [3:0] Rd_2
);

  Register #(.width(22)) register_1 (
    .D({Rd, Mem_Data, ALU_Data, RW_RSrc}), .en(1'b1), .Q({Rd_2, Mem_Data_2, ALU_Data_2, RegW_RegDataSrc}),
    .clk(Clock), .clr(Reset));
endmodule
